# Fritzing sketch SoundbarController (saved by Fritzing 0.9.3b)
circuit board: 4.03564cm x 4.82763cm

parts:
  WeMos_D1_Mini = WeMos D1 Mini
  IR_LED = LED - 3mm [color="Red (633nm)" package="3 mm [THT]"]
  100Ω = Resistor [tolerance=±5% resistance=100 package="2010 [SMD]"]
  IR_Receiver = IR_Receiver

nets:
  3V3: WeMos_D1_Mini.3V3, IR_Receiver.VCC
  N1: WeMos_D1_Mini.D1, 100Ω.Pin_0
  N2: WeMos_D1_Mini.D7, IR_Receiver.OUT
  N3: WeMos_D1_Mini.D8, WeMos_D1_Mini.G, IR_LED.cathode, IR_Receiver.GND
  N4: IR_LED.anode, 100Ω.Pin_1

custom parts:
  IR_Receiver: 赤外線受信モジュール GP1UXC41QS
